# Fritzing sketch instrumento1_ohmimetro (saved by Fritzing 0.9.3b)
breadboards: 1

parts:
  Part1 = Arduino Uno (Rev3) - ICSP
  R1 = Resistor [tolerance=±5% resistance=1k package=THT]
  R2 = Resistor [tolerance=±5% resistance=1k package=THT]

nets:
  N1: Part1.A0, R1.Pin_1, R2.Pin_0
  N2: Part1.5V, R1.Pin_0
  N3: Part1.GND, R2.Pin_1
