# Fritzing sketch instrumento2_capacimetro (saved by Fritzing 0.9.3b)
breadboards: 1

parts:
  Part1 = Arduino Uno (Rev3)
  C1 = Generic Ceramic Capacitor [capacitance=100nF package="100 mil [THT, multilayer]"]
  R1 = Resistor [tolerance=±5% resistance=220 package=THT]

nets:
  N1: Part1.A0, C1.1, R1.Pin_0
  N2: Part1.D2, R1.Pin_1
  N3: Part1.GND, C1.0
